# Fritzing sketch bubblemeter (saved by Fritzing 1.0.1rc)

parts:
  A1 = Esp32-c3 super mini
  DS1 = DS18B20 1-Wire Temperature Sensor [part_number=DS18B20]
  M1 = fc-51 [package=THT]

nets:
  N1: A1.Pin_9, M1.pin1
  N2: A1.Pin_10, A1.Pin_11, DS1.DQ
  3.3V: A1.Pin_14, DS1.VDD, M1.pin3
  GND: A1.Pin_15, DS1.GND, M1.pin2

notes:
  zf240608.1030
  zf240608.1028

custom parts:
  Esp32-c3 super mini: ESP32-C3 Development Board ESP32 SuperMini Development Board ESP32 Development Board WiFi Bluetooth.
